// Logisim project Devoir_2.circ as structural Verilog: 3 circuits, main circuit EXO1
module EXO1 (
  input  in_1,
  input  [3:0] Mot,
  input  DL,
  output [3:0] out_4
);

  wire and_1_out, and_2_out, and_3_out, and_4_out, and_5_out, and_6_out, and_7_out, and_8_out, and_9_out,
       and_10_out, clock_1_out, j_k_ff_1_q, j_k_ff_1_qn, j_k_ff_2_q, j_k_ff_2_qn, j_k_ff_3_q, j_k_ff_3_qn,
       j_k_ff_4_q, j_k_ff_4_qn, j_k_ff_5_q, j_k_ff_5_qn;
  wire [3:0] register_1_q, register_2_q, register_3_q, register_4_q;

  LED led_1 (.in(in_1));
  Clock clock_1 (.out(clock_1_out));
  LED led_2 (.in(DL));
  and and_1 (and_1_out, in_1, j_k_ff_1_qn);
  Register #(.width(4)) register_1 (.D(Mot), .en(and_1_out), .Q(register_1_q), .clk(clock_1_out));  // open: clr
  LED led_3 (.in(j_k_ff_1_q));
  J_K_Flip_Flop j_k_ff_1 (
    .J(and_1_out), .clk(clock_1_out), .K(and_2_out), .Q(j_k_ff_1_q), .Qn(j_k_ff_1_qn));  // open: preset, en, reset
  and and_2 (and_2_out, j_k_ff_1_q, j_k_ff_2_qn);
  Register #(.width(4)) register_2 (
    .D(register_1_q), .en(and_3_out), .Q(register_2_q), .clk(clock_1_out));  // open: clr
  and and_3 (and_3_out, j_k_ff_2_qn, j_k_ff_1_q);
  and and_4 (and_4_out, j_k_ff_3_qn, j_k_ff_2_q);
  J_K_Flip_Flop j_k_ff_2 (
    .J(and_3_out), .clk(clock_1_out), .K(and_5_out), .Q(j_k_ff_2_q), .Qn(j_k_ff_2_qn));  // open: preset, en, reset
  LED led_4 (.in(j_k_ff_2_q));
  and and_5 (and_5_out, j_k_ff_2_q, j_k_ff_3_qn);
  Register #(.width(4)) register_3 (
    .D(register_2_q), .en(and_4_out), .Q(register_3_q), .clk(clock_1_out));  // open: clr
  J_K_Flip_Flop j_k_ff_3 (
    .J(and_4_out), .clk(clock_1_out), .K(and_6_out), .Q(j_k_ff_3_q), .Qn(j_k_ff_3_qn));  // open: preset, en, reset
  and and_6 (and_6_out, j_k_ff_3_q, j_k_ff_4_qn);
  and and_7 (and_7_out, j_k_ff_3_q, j_k_ff_4_qn);
  Register #(.width(4)) register_4 (
    .D(register_3_q), .en(and_7_out), .Q(register_4_q), .clk(clock_1_out));  // open: clr
  J_K_Flip_Flop j_k_ff_4 (
    .J(and_7_out), .clk(clock_1_out), .K(and_8_out), .Q(j_k_ff_4_q), .Qn(j_k_ff_4_qn));  // open: preset, en, reset
  LED led_5 (.in(j_k_ff_4_q));
  and and_8 (and_8_out, j_k_ff_4_q, j_k_ff_5_qn);
  and and_9 (and_9_out, j_k_ff_5_qn, j_k_ff_4_q);
  Register #(.width(4)) register_5 (.D(register_4_q), .en(and_9_out), .Q(out_4), .clk(clock_1_out));  // open: clr
  LED led_6 (.in(j_k_ff_5_q));
  J_K_Flip_Flop j_k_ff_5 (
    .J(and_9_out), .clk(clock_1_out), .K(and_10_out), .Q(j_k_ff_5_q), .Qn(j_k_ff_5_qn));  // open: preset, en, reset
  and and_10 (and_10_out, DL, j_k_ff_5_q);
  LED led_7 (.in(j_k_ff_5_q));
  LED led_8 (.in(j_k_ff_1_qn));
  LED led_9 (.in(and_1_out));
  LED led_10 (.in(and_10_out));

  // Notes on the sheet:
  //   DE
  //   SP
  //   EP
  //   E
  //   L
endmodule

module Exo3 (
  input  DE,
  input  [3:0] le_mot,
  input  DL,
  output [3:0] out_4
);

  wire and_1_out, and_2_out, and_3_out, and_4_out, and_5_out, and_6_out, and_7_out, and_8_out, and_9_out,
       and_10_out, clock_1_out, d_ff_1_q, d_ff_2_q, d_ff_3_q, d_ff_4_q, E_out, j_k_ff_1_q, j_k_ff_1_qn,
       j_k_ff_2_q, j_k_ff_2_qn, j_k_ff_3_q, j_k_ff_3_qn, j_k_ff_4_q, j_k_ff_4_qn, L_out, not_1_out,
       not_2_out, not_3_out, not_4_out, or_1_out, or_2_out, or_3_out, or_4_out, P_out, R_out;
  wire [3:0] controlled_buffer_1_out, register_1_q, register_2_q, register_3_q, register_4_q;

  LED led_1 (.in(DL));
  Clock clock_1 (.out(clock_1_out));
  LED led_2 (.in(DE));
  assign controlled_buffer_1_out = E_out ? le_mot : 4'bz;  // Controlled_Buffer controlled_buffer_1
  and and_1 (and_1_out, j_k_ff_2_qn, j_k_ff_1_q);
  not not_1 (not_1_out, R_out);
  D_Flip_Flop d_ff_1 (.clk(clock_1_out), .Q(d_ff_1_q));  // open: D, Qn, preset, en, reset
  Register #(.width(4)) register_1 (
    .D(controlled_buffer_1_out), .en(or_1_out), .Q(register_1_q), .clk(clock_1_out));  // open: clr
  J_K_Flip_Flop j_k_ff_1 (
    .J(or_1_out), .clk(clock_1_out), .K(and_1_out), .Q(j_k_ff_1_q), .Qn(j_k_ff_1_qn));  // open: preset, en, reset
  LED led_3 (.in(E_out));
  and E (E_out, j_k_ff_1_qn, DE, not_1_out);
  and L (L_out, DL, j_k_ff_4_q, or_4_out);
  LED led_4 (.in(j_k_ff_1_qn));
  LED led_5 (.in(L_out));
  or or_1 (or_1_out, R_out, E_out);
  and and_2 (and_2_out, d_ff_1_q, j_k_ff_1_q);
  and and_3 (and_3_out, j_k_ff_2_qn, j_k_ff_1_q);
  and and_4 (and_4_out, j_k_ff_3_qn, j_k_ff_2_q);
  LED led_6 ();  // open: in
  and R (R_out, j_k_ff_4_q, j_k_ff_1_qn, or_3_out, not_2_out);
  D_Flip_Flop d_ff_2 (.clk(clock_1_out), .Q(d_ff_2_q));  // open: D, Qn, preset, en, reset
  Register #(.width(4)) register_2 (
    .D(register_1_q), .en(and_3_out), .Q(register_2_q), .clk(clock_1_out));  // open: clr
  J_K_Flip_Flop j_k_ff_2 (
    .J(and_3_out), .clk(clock_1_out), .K(and_4_out), .Q(j_k_ff_2_q), .Qn(j_k_ff_2_qn));  // open: preset, en, reset
  and and_5 (and_5_out, d_ff_2_q, j_k_ff_2_q);
  and and_6 (and_6_out, j_k_ff_3_qn, j_k_ff_2_q);
  and and_7 (and_7_out, j_k_ff_4_qn, j_k_ff_3_q);
  D_Flip_Flop d_ff_3 (.clk(clock_1_out), .Q(d_ff_3_q));  // open: D, Qn, preset, en, reset
  Register #(.width(4)) register_3 (
    .D(register_2_q), .en(and_6_out), .Q(register_3_q), .clk(clock_1_out));  // open: clr
  J_K_Flip_Flop j_k_ff_3 (
    .J(and_6_out), .clk(clock_1_out), .K(and_7_out), .Q(j_k_ff_3_q), .Qn(j_k_ff_3_qn));  // open: preset, en, reset
  or or_2 (or_2_out, R_out, L_out);
  assign controlled_buffer_1_out = R_out ? register_4_q : 4'bz;  // Controlled_Buffer controlled_buffer_2
  and and_8 (and_8_out, d_ff_3_q, j_k_ff_3_q);
  D_Flip_Flop d_ff_4 (.clk(clock_1_out), .Q(d_ff_4_q));  // open: D, Qn, preset, en, reset
  Register #(.width(4)) register_4 (
    .D(register_3_q), .en(and_9_out), .Q(register_4_q), .clk(clock_1_out));  // open: clr
  and and_9 (and_9_out, j_k_ff_4_qn, j_k_ff_3_q);
  J_K_Flip_Flop j_k_ff_4 (
    .J(and_9_out), .clk(clock_1_out), .K(or_2_out), .Q(j_k_ff_4_q), .Qn(j_k_ff_4_qn));  // open: preset, en, reset
  LED led_7 (.in(j_k_ff_4_q));
  or or_3 (or_3_out, and_2_out, and_5_out, and_8_out, P_out);
  LED led_8 (.in(or_3_out));
  and P (P_out, d_ff_4_q, j_k_ff_4_q);
  LED led_9 (.in(P_out));
  not not_2 (not_2_out, P_out);
  assign out_4 = L_out ? register_4_q : 4'bz;  // Controlled_Buffer controlled_buffer_3
  not not_3 (not_3_out, or_3_out);
  and and_10 (and_10_out, not_3_out, not_4_out);
  not not_4 (not_4_out, P_out);
  or or_4 (or_4_out, and_10_out, P_out);

  // Notes on the sheet:
  //   0
  //   priorité
  //   etage0
  //   BP0
  //   EP
  //   priorité
  //   1
  //   etage1
  //   PB1
  //   2
  //   prioreté
  //   etage2
  //   BP2
  //   3
  //   prioreté
  //   etage3
  //   BP3
  //   SP
  //   PG
endmodule

module Exo2 (
  input  DE,
  input  DL,
  input  in_3,
  input  Bit_d_entree0,
  input  in_5,
  input  Bit_d_entree1,
  input  in_7,
  input  Bit_d_entree2,
  input  in_9,
  input  Bit_d_entree3
);

  wire clock_1_out, controlled_buffer_1_out, controlled_buffer_2_out, controlled_buffer_3_out,
       controlled_buffer_4_out, controlled_buffer_5_out, controlled_buffer_6_out, controlled_buffer_7_out,
       controlled_buffer_8_out, controlled_buffer_9_out, controlled_buffer_11_out, controlled_buffer_13_out,
       controlled_buffer_15_out, controlled_buffer_17_out, controlled_buffer_21_out,
       controlled_buffer_22_out, controlled_buffer_23_out, controlled_buffer_25_out,
       controlled_buffer_27_out, controlled_buffer_29_out, controlled_buffer_31_out,
       controlled_buffer_33_out, controlled_buffer_34_out, controlled_buffer_35_out,
       controlled_buffer_36_out, d_ff_5_q, d_ff_6_q, d_ff_7_q, d_ff_8_q, d_ff_9_q, d_ff_10_q, d_ff_11_q,
       d_ff_12_q, d_ff_13_q, d_ff_14_q, d_ff_15_q, d_ff_16_q, d_ff_17_q, d_ff_18_q, d_ff_19_q, d_ff_20_q,
       d_ff_21_q, d_ff_22_q, d_ff_23_q, d_ff_24_q, d_ff_24_qn, E_out, L_out, not_1_out;

  Clock clock_1 (.out(clock_1_out));
  not not_1 (not_1_out, DL);
  D_Flip_Flop d_ff_1 (.clk(clock_1_out), .D(controlled_buffer_1_out));  // open: Q, Qn, preset, en, reset
  D_Flip_Flop d_ff_2 (.clk(clock_1_out), .D(controlled_buffer_3_out));  // open: Q, Qn, preset, en, reset
  D_Flip_Flop d_ff_3 (.clk(clock_1_out), .D(controlled_buffer_5_out));  // open: Q, Qn, preset, en, reset
  D_Flip_Flop d_ff_4 (.clk(clock_1_out), .D(controlled_buffer_7_out));  // open: Q, Qn, preset, en, reset
  LED led_1 (.in(E_out));
  and E (E_out, DE, d_ff_24_qn, not_1_out);
  LED led_2 (.in(L_out));
  and L (L_out, DL, d_ff_9_q);
  assign controlled_buffer_1_out = L_out ? d_ff_5_q : 1'bz;  // Controlled_Buffer controlled_buffer_1
  assign controlled_buffer_2_out = E_out ? Bit_d_entree0 : 1'bz;  // Controlled_Buffer controlled_buffer_2
  assign controlled_buffer_3_out = L_out ? d_ff_6_q : 1'bz;  // Controlled_Buffer controlled_buffer_3
  assign controlled_buffer_4_out = E_out ? Bit_d_entree1 : 1'bz;  // Controlled_Buffer controlled_buffer_4
  assign controlled_buffer_5_out = L_out ? d_ff_7_q : 1'bz;  // Controlled_Buffer controlled_buffer_5
  assign controlled_buffer_6_out = E_out ? Bit_d_entree2 : 1'bz;  // Controlled_Buffer controlled_buffer_6
  assign controlled_buffer_7_out = L_out ? d_ff_8_q : 1'bz;  // Controlled_Buffer controlled_buffer_7
  assign controlled_buffer_8_out = E_out ? Bit_d_entree3 : 1'bz;  // Controlled_Buffer controlled_buffer_8
  assign controlled_buffer_9_out = E_out ? 1'b1 : 1'bz;  // Controlled_Buffer controlled_buffer_9
  assign controlled_buffer_2_out = L_out ? d_ff_10_q : 1'bz;  // Controlled_Buffer controlled_buffer_10
  D_Flip_Flop d_ff_5 (.clk(clock_1_out), .D(controlled_buffer_2_out), .Q(d_ff_5_q));  // open: Qn, preset, en, reset
  assign controlled_buffer_11_out = E_out ? d_ff_5_q : 1'bz;  // Controlled_Buffer controlled_buffer_11
  assign controlled_buffer_4_out = L_out ? d_ff_11_q : 1'bz;  // Controlled_Buffer controlled_buffer_12
  assign controlled_buffer_13_out = E_out ? d_ff_6_q : 1'bz;  // Controlled_Buffer controlled_buffer_13
  D_Flip_Flop d_ff_6 (.clk(clock_1_out), .D(controlled_buffer_4_out), .Q(d_ff_6_q));  // open: Qn, preset, en, reset
  assign controlled_buffer_6_out = L_out ? d_ff_12_q : 1'bz;  // Controlled_Buffer controlled_buffer_14
  assign controlled_buffer_15_out = E_out ? d_ff_7_q : 1'bz;  // Controlled_Buffer controlled_buffer_15
  D_Flip_Flop d_ff_7 (.clk(clock_1_out), .D(controlled_buffer_6_out), .Q(d_ff_7_q));  // open: Qn, preset, en, reset
  assign controlled_buffer_8_out = L_out ? d_ff_13_q : 1'bz;  // Controlled_Buffer controlled_buffer_16
  assign controlled_buffer_17_out = E_out ? d_ff_8_q : 1'bz;  // Controlled_Buffer controlled_buffer_17
  D_Flip_Flop d_ff_8 (.clk(clock_1_out), .D(controlled_buffer_8_out), .Q(d_ff_8_q));  // open: Qn, preset, en, reset
  assign controlled_buffer_9_out = L_out ? d_ff_14_q : 1'bz;  // Controlled_Buffer controlled_buffer_18
  D_Flip_Flop d_ff_9 (.clk(clock_1_out), .D(controlled_buffer_9_out), .Q(d_ff_9_q));  // open: Qn, preset, en, reset
  assign controlled_buffer_11_out = L_out ? d_ff_15_q : 1'bz;  // Controlled_Buffer controlled_buffer_19
  D_Flip_Flop d_ff_10 (.clk(clock_1_out), .D(controlled_buffer_11_out), .Q(d_ff_10_q));  // open: Qn, preset, en, reset
  assign controlled_buffer_13_out = L_out ? d_ff_16_q : 1'bz;  // Controlled_Buffer controlled_buffer_20
  D_Flip_Flop d_ff_11 (.clk(clock_1_out), .D(controlled_buffer_13_out), .Q(d_ff_11_q));  // open: Qn, preset, en, reset
  D_Flip_Flop d_ff_12 (.clk(clock_1_out), .D(controlled_buffer_15_out), .Q(d_ff_12_q));  // open: Qn, preset, en, reset
  D_Flip_Flop d_ff_13 (.clk(clock_1_out), .D(controlled_buffer_17_out), .Q(d_ff_13_q));  // open: Qn, preset, en, reset
  D_Flip_Flop d_ff_14 (.clk(clock_1_out), .D(controlled_buffer_21_out), .Q(d_ff_14_q));  // open: Qn, preset, en, reset
  assign controlled_buffer_21_out = E_out ? d_ff_9_q : 1'bz;  // Controlled_Buffer controlled_buffer_21
  D_Flip_Flop d_ff_15 (.clk(clock_1_out), .D(controlled_buffer_22_out), .Q(d_ff_15_q));  // open: Qn, preset, en, reset
  assign controlled_buffer_22_out = E_out ? d_ff_10_q : 1'bz;  // Controlled_Buffer controlled_buffer_22
  D_Flip_Flop d_ff_16 (.clk(clock_1_out), .D(controlled_buffer_23_out), .Q(d_ff_16_q));  // open: Qn, preset, en, reset
  assign controlled_buffer_23_out = E_out ? d_ff_11_q : 1'bz;  // Controlled_Buffer controlled_buffer_23
  assign controlled_buffer_15_out = L_out ? d_ff_17_q : 1'bz;  // Controlled_Buffer controlled_buffer_24
  assign controlled_buffer_25_out = E_out ? d_ff_12_q : 1'bz;  // Controlled_Buffer controlled_buffer_25
  assign controlled_buffer_17_out = L_out ? d_ff_18_q : 1'bz;  // Controlled_Buffer controlled_buffer_26
  assign controlled_buffer_27_out = E_out ? d_ff_13_q : 1'bz;  // Controlled_Buffer controlled_buffer_27
  assign controlled_buffer_21_out = L_out ? d_ff_19_q : 1'bz;  // Controlled_Buffer controlled_buffer_28
  assign controlled_buffer_29_out = E_out ? d_ff_14_q : 1'bz;  // Controlled_Buffer controlled_buffer_29
  assign controlled_buffer_22_out = L_out ? d_ff_20_q : 1'bz;  // Controlled_Buffer controlled_buffer_30
  assign controlled_buffer_31_out = E_out ? d_ff_15_q : 1'bz;  // Controlled_Buffer controlled_buffer_31
  assign controlled_buffer_23_out = L_out ? d_ff_21_q : 1'bz;  // Controlled_Buffer controlled_buffer_32
  assign controlled_buffer_33_out = E_out ? d_ff_16_q : 1'bz;  // Controlled_Buffer controlled_buffer_33
  assign controlled_buffer_34_out = E_out ? d_ff_17_q : 1'bz;  // Controlled_Buffer controlled_buffer_34
  D_Flip_Flop d_ff_17 (.clk(clock_1_out), .D(controlled_buffer_25_out), .Q(d_ff_17_q));  // open: Qn, preset, en, reset
  D_Flip_Flop d_ff_18 (.clk(clock_1_out), .D(controlled_buffer_27_out), .Q(d_ff_18_q));  // open: Qn, preset, en, reset
  assign controlled_buffer_35_out = E_out ? d_ff_18_q : 1'bz;  // Controlled_Buffer controlled_buffer_35
  D_Flip_Flop d_ff_19 (.clk(clock_1_out), .D(controlled_buffer_29_out), .Q(d_ff_19_q));  // open: Qn, preset, en, reset
  assign controlled_buffer_36_out = E_out ? d_ff_19_q : 1'bz;  // Controlled_Buffer controlled_buffer_36
  assign controlled_buffer_31_out = L_out ? in_3 : 1'bz;  // Controlled_Buffer controlled_buffer_37
  D_Flip_Flop d_ff_20 (.clk(clock_1_out), .D(controlled_buffer_31_out), .Q(d_ff_20_q));  // open: Qn, preset, en, reset
  assign controlled_buffer_33_out = L_out ? in_5 : 1'bz;  // Controlled_Buffer controlled_buffer_38
  D_Flip_Flop d_ff_21 (.clk(clock_1_out), .D(controlled_buffer_33_out), .Q(d_ff_21_q));  // open: Qn, preset, en, reset
  assign controlled_buffer_25_out = L_out ? d_ff_22_q : 1'bz;  // Controlled_Buffer controlled_buffer_39
  assign controlled_buffer_34_out = L_out ? in_7 : 1'bz;  // Controlled_Buffer controlled_buffer_40
  D_Flip_Flop d_ff_22 (.clk(clock_1_out), .D(controlled_buffer_34_out), .Q(d_ff_22_q));  // open: Qn, preset, en, reset
  assign controlled_buffer_27_out = L_out ? d_ff_23_q : 1'bz;  // Controlled_Buffer controlled_buffer_41
  assign controlled_buffer_35_out = L_out ? in_9 : 1'bz;  // Controlled_Buffer controlled_buffer_42
  D_Flip_Flop d_ff_23 (.clk(clock_1_out), .D(controlled_buffer_35_out), .Q(d_ff_23_q));  // open: Qn, preset, en, reset
  assign controlled_buffer_29_out = L_out ? d_ff_24_q : 1'bz;  // Controlled_Buffer controlled_buffer_43
  assign controlled_buffer_36_out = L_out ? 1'b0 : 1'bz;  // Controlled_Buffer controlled_buffer_44
  D_Flip_Flop d_ff_24 (
    .clk(clock_1_out), .D(controlled_buffer_36_out), .Q(d_ff_24_q), .Qn(d_ff_24_qn));  // open: preset, en, reset

  // Notes on the sheet:
  //   Bit de sortie2
  //   Bit de sortie3
  //   Bit de sortie0
  //   Bit de sortie1
  //   Registre de présance
endmodule
