// Logisim project Devoir_entree_sortie.circ as structural Verilog: 1 circuit, main circuit entree sortie
module entree_sortie (
  input  e0,
  input  e1,
  input  e2,
  input  P7,
  input  P6,
  input  P5,
  input  P4,
  input  P3,
  input  P2,
  input  P1,
  input  P0,
  input  E,
  output i,
  output A15,
  output A14,
  output A13,
  output A12,
  output A11,
  output A10,
  output A9,
  output A8,
  output A7,
  output A6,
  output A5,
  output A4,
  output A3,
  output A2,
  output A1,
  output A0
);

  wire and_1_out, comparator_1_gt, decoder_1_out0, decoder_1_out1, decoder_1_out2, decoder_1_out3,
       decoder_1_out4, decoder_1_out5, decoder_1_out6, decoder_1_out7, priority_encoder_1_gs,
       pull_resistor_1_node, pull_resistor_2_node, pull_resistor_3_node, pull_resistor_4_node,
       pull_resistor_5_node, pull_resistor_7_node, pull_resistor_9_node, pull_resistor_11_node,
       pull_resistor_13_node, pull_resistor_15_node, pull_resistor_16_node, transistor_24_out,
       transistor_33_out, transistor_42_out, transistor_49_out, transistor_60_out;
  wire [2:0] not_1_out, priority_encoder_1_out;

  Priority_Encoder priority_encoder_1 (
    .in0(P7), .in1(P6), .in2(P5), .in3(P4), .in4(P3), .in5(P2), .in6(P1), .in7(P0),
    .out(priority_encoder_1_out), .en_in(1'b1), .gs(priority_encoder_1_gs));  // open: en_out
  not not_1 (not_1_out[0], priority_encoder_1_out[0]);
  not not_2 (not_1_out[1], priority_encoder_1_out[1]);
  not not_3 (not_1_out[2], priority_encoder_1_out[2]);
  Comparator #(.width(3), .mode("unsigned")) comparator_1 (
    .a({e2, e1, e0}), .b(not_1_out), .gt(comparator_1_gt));  // open: eq, lt
  and and_1 (and_1_out, priority_encoder_1_gs, E);
  assign i = and_1_out ? comparator_1_gt : 1'bz;  // Controlled_Buffer controlled_buffer_1
  Decoder #(.select(3), .enable("false")) decoder_1 (
    .out0(decoder_1_out0), .out1(decoder_1_out1), .out2(decoder_1_out2), .out3(decoder_1_out3),
    .out4(decoder_1_out4), .out5(decoder_1_out5), .out6(decoder_1_out6), .out7(decoder_1_out7),
    .sel(not_1_out));
  Pull_Resistor pull_resistor_1 (.node(pull_resistor_1_node));
  Transistor #(.\type ("n")) transistor_1 (.in(1'b1), .out(pull_resistor_1_node), .gate(decoder_1_out1));
  Transistor #(.\type ("n")) transistor_2 (.in(1'b1), .out(pull_resistor_1_node), .gate(decoder_1_out2));
  Transistor #(.\type ("n")) transistor_3 (.in(1'b1), .out(pull_resistor_1_node), .gate(decoder_1_out4));
  Transistor #(.\type ("n")) transistor_4 (.in(1'b1), .out(pull_resistor_1_node), .gate(decoder_1_out7));
  assign A15 = i ? pull_resistor_1_node : 1'bz;  // Controlled_Buffer controlled_buffer_2
  Pull_Resistor pull_resistor_2 (.node(pull_resistor_2_node));
  Transistor #(.\type ("n")) transistor_5 (.in(1'b1), .out(pull_resistor_2_node), .gate(decoder_1_out3));
  Transistor #(.\type ("n")) transistor_6 (.in(1'b1), .out(pull_resistor_2_node), .gate(decoder_1_out5));
  Transistor #(.\type ("n")) transistor_7 (.in(1'b1), .out(pull_resistor_2_node), .gate(decoder_1_out6));
  Transistor #(.\type ("n")) transistor_8 (.in(1'b1), .out(pull_resistor_2_node), .gate(decoder_1_out7));
  assign A14 = i ? pull_resistor_2_node : 1'bz;  // Controlled_Buffer controlled_buffer_3
  Pull_Resistor pull_resistor_3 (.node(pull_resistor_3_node));
  Transistor #(.\type ("n")) transistor_9 (.in(1'b1), .out(pull_resistor_3_node), .gate(decoder_1_out2));
  Transistor #(.\type ("n")) transistor_10 (.in(1'b1), .out(pull_resistor_3_node), .gate(decoder_1_out3));
  Transistor #(.\type ("n")) transistor_11 (.in(1'b1), .out(pull_resistor_3_node), .gate(decoder_1_out4));
  Transistor #(.\type ("n")) transistor_12 (.in(1'b1), .out(pull_resistor_3_node), .gate(decoder_1_out5));
  Transistor #(.\type ("n")) transistor_13 (.in(1'b1), .out(pull_resistor_3_node), .gate(decoder_1_out6));
  Transistor #(.\type ("n")) transistor_14 (.in(1'b1), .out(pull_resistor_3_node), .gate(decoder_1_out7));
  assign A13 = i ? pull_resistor_3_node : 1'bz;  // Controlled_Buffer controlled_buffer_4
  Pull_Resistor pull_resistor_4 (.node(pull_resistor_4_node));
  Transistor #(.\type ("n")) transistor_15 (.in(1'b1), .out(pull_resistor_4_node), .gate(decoder_1_out0));
  Transistor #(.\type ("n")) transistor_16 (.in(1'b1), .out(pull_resistor_4_node), .gate(decoder_1_out4));
  Transistor #(.\type ("n")) transistor_17 (.in(1'b1), .out(pull_resistor_4_node), .gate(decoder_1_out6));
  Transistor #(.\type ("n")) transistor_18 (.in(1'b1), .out(pull_resistor_4_node), .gate(decoder_1_out7));
  assign A12 = i ? pull_resistor_4_node : 1'bz;  // Controlled_Buffer controlled_buffer_5
  Pull_Resistor pull_resistor_5 (.node(pull_resistor_5_node));
  Transistor #(.\type ("n")) transistor_19 (.in(1'b1), .out(pull_resistor_5_node), .gate(decoder_1_out0));
  Transistor #(.\type ("n")) transistor_20 (.in(1'b1), .out(pull_resistor_5_node), .gate(decoder_1_out1));
  Transistor #(.\type ("n")) transistor_21 (.in(1'b1), .out(pull_resistor_5_node), .gate(decoder_1_out2));
  Transistor #(.\type ("n")) transistor_22 (.in(1'b1), .out(pull_resistor_5_node), .gate(decoder_1_out3));
  Transistor #(.\type ("n")) transistor_23 (.in(1'b1), .out(pull_resistor_5_node), .gate(decoder_1_out5));
  assign A11 = i ? pull_resistor_5_node : 1'bz;  // Controlled_Buffer controlled_buffer_6
  Transistor #(.\type ("n")) transistor_24 (.in(1'b1), .out(transistor_24_out), .gate(decoder_1_out1));
  Transistor #(.\type ("n")) transistor_25 (.in(1'b1), .out(transistor_24_out), .gate(decoder_1_out2));
  Transistor #(.\type ("n")) transistor_26 (.in(1'b1), .out(transistor_24_out), .gate(decoder_1_out7));
  Pull_Resistor pull_resistor_6 (.node(transistor_24_out));
  Transistor #(.\type ("n")) transistor_27 (.in(1'b1), .out(transistor_24_out), .gate(decoder_1_out4));
  assign A10 = i ? transistor_24_out : 1'bz;  // Controlled_Buffer controlled_buffer_7
  Pull_Resistor pull_resistor_7 (.node(pull_resistor_7_node));
  Transistor #(.\type ("n")) transistor_28 (.in(1'b1), .out(pull_resistor_7_node), .gate(decoder_1_out1));
  Transistor #(.\type ("n")) transistor_29 (.in(1'b1), .out(pull_resistor_7_node), .gate(decoder_1_out3));
  Transistor #(.\type ("n")) transistor_30 (.in(1'b1), .out(pull_resistor_7_node), .gate(decoder_1_out5));
  Transistor #(.\type ("n")) transistor_31 (.in(1'b1), .out(pull_resistor_7_node), .gate(decoder_1_out6));
  Transistor #(.\type ("n")) transistor_32 (.in(1'b1), .out(pull_resistor_7_node), .gate(decoder_1_out7));
  assign A9 = i ? pull_resistor_7_node : 1'bz;  // Controlled_Buffer controlled_buffer_8
  Transistor #(.\type ("n")) transistor_33 (.in(1'b1), .out(transistor_33_out), .gate(decoder_1_out2));
  Transistor #(.\type ("n")) transistor_34 (.in(1'b1), .out(transistor_33_out), .gate(decoder_1_out3));
  Transistor #(.\type ("n")) transistor_35 (.in(1'b1), .out(transistor_33_out), .gate(decoder_1_out4));
  Transistor #(.\type ("n")) transistor_36 (.in(1'b1), .out(transistor_33_out), .gate(decoder_1_out5));
  Transistor #(.\type ("n")) transistor_37 (.in(1'b1), .out(transistor_33_out), .gate(decoder_1_out6));
  Transistor #(.\type ("n")) transistor_38 (.in(1'b1), .out(transistor_33_out), .gate(decoder_1_out7));
  Pull_Resistor pull_resistor_8 (.node(transistor_33_out));
  assign A8 = i ? transistor_33_out : 1'bz;  // Controlled_Buffer controlled_buffer_9
  Pull_Resistor pull_resistor_9 (.node(pull_resistor_9_node));
  Transistor #(.\type ("n")) transistor_39 (.in(1'b1), .out(pull_resistor_9_node), .gate(decoder_1_out3));
  Transistor #(.\type ("n")) transistor_40 (.in(1'b1), .out(pull_resistor_9_node), .gate(decoder_1_out6));
  Transistor #(.\type ("n")) transistor_41 (.in(1'b1), .out(pull_resistor_9_node), .gate(decoder_1_out7));
  assign A7 = i ? pull_resistor_9_node : 1'bz;  // Controlled_Buffer controlled_buffer_10
  Transistor #(.\type ("n")) transistor_42 (.in(1'b1), .out(transistor_42_out), .gate(decoder_1_out1));
  Transistor #(.\type ("n")) transistor_43 (.in(1'b1), .out(transistor_42_out), .gate(decoder_1_out2));
  Transistor #(.\type ("n")) transistor_44 (.in(1'b1), .out(transistor_42_out), .gate(decoder_1_out5));
  Pull_Resistor pull_resistor_10 (.node(transistor_42_out));
  Transistor #(.\type ("n")) transistor_45 (.in(1'b1), .out(transistor_42_out), .gate(decoder_1_out0));
  Transistor #(.\type ("n")) transistor_46 (.in(1'b1), .out(transistor_42_out), .gate(decoder_1_out3));
  assign A6 = i ? transistor_42_out : 1'bz;  // Controlled_Buffer controlled_buffer_11
  Pull_Resistor pull_resistor_11 (.node(pull_resistor_11_node));
  Transistor #(.\type ("n")) transistor_47 (.in(1'b1), .out(pull_resistor_11_node), .gate(decoder_1_out4));
  Transistor #(.\type ("n")) transistor_48 (.in(1'b1), .out(pull_resistor_11_node), .gate(decoder_1_out7));
  assign A5 = i ? pull_resistor_11_node : 1'bz;  // Controlled_Buffer controlled_buffer_12
  Transistor #(.\type ("n")) transistor_49 (.in(1'b1), .out(transistor_49_out), .gate(decoder_1_out1));
  Transistor #(.\type ("n")) transistor_50 (.in(1'b1), .out(transistor_49_out), .gate(decoder_1_out3));
  Transistor #(.\type ("n")) transistor_51 (.in(1'b1), .out(transistor_49_out), .gate(decoder_1_out5));
  Transistor #(.\type ("n")) transistor_52 (.in(1'b1), .out(transistor_49_out), .gate(decoder_1_out6));
  Transistor #(.\type ("n")) transistor_53 (.in(1'b1), .out(transistor_49_out), .gate(decoder_1_out7));
  Pull_Resistor pull_resistor_12 (.node(transistor_49_out));
  assign A4 = i ? transistor_49_out : 1'bz;  // Controlled_Buffer controlled_buffer_13
  Pull_Resistor pull_resistor_13 (.node(pull_resistor_13_node));
  Transistor #(.\type ("n")) transistor_54 (.in(1'b1), .out(pull_resistor_13_node), .gate(decoder_1_out2));
  Transistor #(.\type ("n")) transistor_55 (.in(1'b1), .out(pull_resistor_13_node), .gate(decoder_1_out3));
  Transistor #(.\type ("n")) transistor_56 (.in(1'b1), .out(pull_resistor_13_node), .gate(decoder_1_out4));
  Transistor #(.\type ("n")) transistor_57 (.in(1'b1), .out(pull_resistor_13_node), .gate(decoder_1_out5));
  Transistor #(.\type ("n")) transistor_58 (.in(1'b1), .out(pull_resistor_13_node), .gate(decoder_1_out6));
  Transistor #(.\type ("n")) transistor_59 (.in(1'b1), .out(pull_resistor_13_node), .gate(decoder_1_out7));
  assign A3 = i ? pull_resistor_13_node : 1'bz;  // Controlled_Buffer controlled_buffer_14
  Transistor #(.\type ("n")) transistor_60 (.in(1'b1), .out(transistor_60_out), .gate(decoder_1_out6));
  Transistor #(.\type ("n")) transistor_61 (.in(1'b1), .out(transistor_60_out), .gate(decoder_1_out7));
  Pull_Resistor pull_resistor_14 (.node(transistor_60_out));
  assign A2 = i ? transistor_60_out : 1'bz;  // Controlled_Buffer controlled_buffer_15
  Pull_Resistor pull_resistor_15 (.node(pull_resistor_15_node));
  Transistor #(.\type ("n")) transistor_62 (.in(1'b1), .out(pull_resistor_15_node), .gate(decoder_1_out0));
  Transistor #(.\type ("n")) transistor_63 (.in(1'b1), .out(pull_resistor_15_node), .gate(decoder_1_out1));
  Transistor #(.\type ("n")) transistor_64 (.in(1'b1), .out(pull_resistor_15_node), .gate(decoder_1_out2));
  Transistor #(.\type ("n")) transistor_65 (.in(1'b1), .out(pull_resistor_15_node), .gate(decoder_1_out3));
  Transistor #(.\type ("n")) transistor_66 (.in(1'b1), .out(pull_resistor_15_node), .gate(decoder_1_out4));
  assign A1 = i ? pull_resistor_15_node : 1'bz;  // Controlled_Buffer controlled_buffer_16
  Pull_Resistor pull_resistor_16 (.node(pull_resistor_16_node));
  Transistor #(.\type ("n")) transistor_67 (.in(1'b1), .out(pull_resistor_16_node), .gate(decoder_1_out1));
  Transistor #(.\type ("n")) transistor_68 (.in(1'b1), .out(pull_resistor_16_node), .gate(decoder_1_out2));
  Transistor #(.\type ("n")) transistor_69 (.in(1'b1), .out(pull_resistor_16_node), .gate(decoder_1_out4));
  Transistor #(.\type ("n")) transistor_70 (.in(1'b1), .out(pull_resistor_16_node), .gate(decoder_1_out7));
  assign A0 = i ? pull_resistor_16_node : 1'bz;  // Controlled_Buffer controlled_buffer_17
endmodule
