// Logisim project Exo1,3,5__TD2.circ as structural Verilog: 3 circuits, main circuit Exo1
module Exo1 (
  input  P3,
  input  P2,
  input  P1
);

  wire decoder_1_out0, decoder_1_out1, decoder_1_out2, decoder_1_out3, decoder_1_out4, decoder_1_out5,
       decoder_1_out6, decoder_1_out7, pull_resistor_2_node, transistor_1_out, transistor_7_out;

  Decoder #(.select(3), .enable("false")) decoder_1 (
    .out0(decoder_1_out0), .out1(decoder_1_out1), .out2(decoder_1_out2), .out3(decoder_1_out3),
    .out4(decoder_1_out4), .out5(decoder_1_out5), .out6(decoder_1_out6), .out7(decoder_1_out7),
    .sel({P1, P2, P3}));
  Transistor #(.\type ("n")) transistor_1 (.in(1'b1), .out(transistor_1_out), .gate(decoder_1_out4));
  Transistor #(.\type ("n")) transistor_2 (.in(1'b1), .out(transistor_1_out), .gate(decoder_1_out5));
  Transistor #(.\type ("n")) transistor_3 (.in(1'b1), .out(transistor_1_out), .gate(decoder_1_out6));
  Transistor #(.\type ("n")) transistor_4 (.in(1'b1), .out(transistor_1_out), .gate(decoder_1_out7));
  Pull_Resistor pull_resistor_1 (.node(transistor_1_out));
  LED u_P1 (.in(transistor_1_out));
  Pull_Resistor pull_resistor_2 (.node(pull_resistor_2_node));
  Transistor #(.\type ("n")) transistor_5 (.in(1'b1), .out(pull_resistor_2_node), .gate(decoder_1_out2));
  Transistor #(.\type ("n")) transistor_6 (.in(1'b1), .out(pull_resistor_2_node), .gate(decoder_1_out3));
  LED u_P2 (.in(pull_resistor_2_node));
  Transistor #(.\type ("n")) transistor_7 (.in(1'b1), .out(transistor_7_out), .gate(decoder_1_out1));
  Pull_Resistor pull_resistor_3 (.node(transistor_7_out));
  LED u_P3 (.in(transistor_7_out));
endmodule

module Exo3 (
  input  G,
  input  D,
  input  A
);

  wire decoder_1_out0, decoder_1_out1, decoder_1_out2, decoder_1_out3, decoder_1_out4, decoder_1_out5,
       decoder_1_out6, decoder_1_out7, pull_resistor_1_node, pull_resistor_3_node, transistor_2_out,
       transistor_6_out;

  Decoder #(.select(3), .enable("false")) decoder_1 (
    .out0(decoder_1_out0), .out1(decoder_1_out1), .out2(decoder_1_out2), .out3(decoder_1_out3),
    .out4(decoder_1_out4), .out5(decoder_1_out5), .out6(decoder_1_out6), .out7(decoder_1_out7),
    .sel({A, D, G}));
  Pull_Resistor pull_resistor_1 (.node(pull_resistor_1_node));
  Transistor #(.\type ("n")) transistor_1 (.in(1'b1), .out(pull_resistor_1_node), .gate(decoder_1_out1));
  LED TD (.in(pull_resistor_1_node));
  Transistor #(.\type ("n")) transistor_2 (.in(1'b1), .out(transistor_2_out), .gate(decoder_1_out2));
  Pull_Resistor pull_resistor_2 (.node(transistor_2_out));
  LED TG (.in(transistor_2_out));
  Pull_Resistor pull_resistor_3 (.node(pull_resistor_3_node));
  Transistor #(.\type ("n")) transistor_3 (.in(1'b1), .out(pull_resistor_3_node), .gate(decoder_1_out0));
  Transistor #(.\type ("n")) transistor_4 (.in(1'b1), .out(pull_resistor_3_node), .gate(decoder_1_out1));
  Transistor #(.\type ("n")) transistor_5 (.in(1'b1), .out(pull_resistor_3_node), .gate(decoder_1_out2));
  LED AV (.in(pull_resistor_3_node));
  Transistor #(.\type ("n")) transistor_6 (.in(1'b1), .out(transistor_6_out), .gate(decoder_1_out3));
  Transistor #(.\type ("n")) transistor_7 (.in(1'b1), .out(transistor_6_out), .gate(decoder_1_out4));
  Transistor #(.\type ("n")) transistor_8 (.in(1'b1), .out(transistor_6_out), .gate(decoder_1_out5));
  Transistor #(.\type ("n")) transistor_9 (.in(1'b1), .out(transistor_6_out), .gate(decoder_1_out6));
  Transistor #(.\type ("n")) transistor_10 (.in(1'b1), .out(transistor_6_out), .gate(decoder_1_out7));
  Pull_Resistor pull_resistor_4 (.node(transistor_6_out));
  LED F (.in(transistor_6_out));
endmodule

module Exo5 (
  input  [3:0] B,
  input  [3:0] A,
  input  [1:0] C,
  output [7:0] ADR,
  output [3:0] RES,
  output Z,
  output D,
  output R
);

  wire decoder_1_out0, decoder_1_out1, decoder_1_out2, decoder_1_out3, decoder_1_out4, decoder_1_out5,
       decoder_1_out6, decoder_1_out7, decoder_2_out0, decoder_2_out1, decoder_2_out2, decoder_2_out3,
       decoder_2_out4, decoder_2_out5, decoder_2_out6, decoder_2_out7, decoder_3_out0, decoder_3_out1,
       decoder_3_out2, decoder_3_out3, decoder_3_out4, decoder_3_out5, decoder_3_out6, decoder_3_out7,
       decoder_4_out0, decoder_4_out1, decoder_4_out2, decoder_4_out3, decoder_4_out4, decoder_4_out5,
       decoder_4_out6, decoder_4_out7, decoder_5_out0, decoder_5_out1, decoder_5_out2, decoder_5_out3;
  wire [0:0] and_1_out, and_2_out, and_3_out;
  wire [4:0] pull_resistor_9_node, pull_resistor_20_node, transistor_33_out, transistor_73_out;

  Multiplexer #(.select(2), .enable("false")) multiplexer_1 (
    .in0(transistor_33_out[0]), .in1(transistor_33_out[1]), .in2(transistor_33_out[2]),
    .in3(transistor_33_out[4]), .out(RES[0]), .sel(C));
  and and_1 (and_1_out[0], transistor_33_out[3], C[0], C[1]);
  Multiplexer #(.select(2), .enable("false")) multiplexer_2 (
    .in0(pull_resistor_9_node[0]), .in1(pull_resistor_9_node[1]), .in2(pull_resistor_9_node[2]),
    .in3(pull_resistor_9_node[4]), .out(RES[1]), .sel(C));
  and and_2 (and_2_out[0], pull_resistor_9_node[3], C[0], C[1]);
  Multiplexer #(.select(2), .enable("false")) multiplexer_3 (
    .in0(pull_resistor_20_node[0]), .in1(pull_resistor_20_node[1]), .in2(pull_resistor_20_node[2]),
    .in3(pull_resistor_20_node[4]), .out(RES[2]), .sel(C));
  and and_3 (and_3_out[0], pull_resistor_20_node[3], C[0], C[1]);
  Multiplexer #(.select(2), .enable("false")) multiplexer_4 (
    .in0(transistor_73_out[0]), .in1(transistor_73_out[1]), .in2(transistor_73_out[2]),
    .in3(transistor_73_out[4]), .out(RES[3]), .sel(C));
  and and_4 (R, transistor_73_out[3], C[0], C[1]);
  Decoder #(.select(3), .enable("false")) decoder_1 (
    .out0(decoder_1_out0), .out1(decoder_1_out1), .out2(decoder_1_out2), .out3(decoder_1_out3),
    .out4(decoder_1_out4), .out5(decoder_1_out5), .out6(decoder_1_out6), .out7(decoder_1_out7),
    .sel({A[1], B[1], and_1_out[0]}));
  Decoder #(.select(3), .enable("false")) decoder_2 (
    .out0(decoder_2_out0), .out1(decoder_2_out1), .out2(decoder_2_out2), .out3(decoder_2_out3),
    .out4(decoder_2_out4), .out5(decoder_2_out5), .out6(decoder_2_out6), .out7(decoder_2_out7),
    .sel({A[0], B[0], 1'b0}));
  nor u_Z (Z, RES[0], RES[1], RES[2], RES[3]);
  xor u_D (D, and_3_out[0], R);
  Pull_Resistor pull_resistor_1 (.node(pull_resistor_9_node[4]));
  Transistor #(.\type ("n")) transistor_1 (.in(1'b1), .out(pull_resistor_9_node[4]), .gate(decoder_1_out1));
  Transistor #(.\type ("n")) transistor_2 (.in(1'b1), .out(pull_resistor_9_node[4]), .gate(decoder_1_out2));
  Transistor #(.\type ("n")) transistor_3 (.in(1'b1), .out(pull_resistor_9_node[4]), .gate(decoder_1_out4));
  Transistor #(.\type ("n")) transistor_4 (.in(1'b1), .out(pull_resistor_9_node[4]), .gate(decoder_1_out7));
  Pull_Resistor pull_resistor_2 (.node(transistor_33_out[4]));
  Transistor #(.\type ("n")) transistor_5 (.in(1'b1), .out(transistor_33_out[4]), .gate(decoder_2_out1));
  Transistor #(.\type ("n")) transistor_6 (.in(1'b1), .out(transistor_33_out[4]), .gate(decoder_2_out2));
  Transistor #(.\type ("n")) transistor_7 (.in(1'b1), .out(transistor_33_out[4]), .gate(decoder_2_out4));
  Transistor #(.\type ("n")) transistor_8 (.in(1'b1), .out(transistor_33_out[4]), .gate(decoder_2_out7));
  Transistor #(.\type ("n")) transistor_9 (.in(1'b1), .out(pull_resistor_9_node[3]), .gate(decoder_1_out3));
  Transistor #(.\type ("n")) transistor_10 (.in(1'b1), .out(pull_resistor_9_node[3]), .gate(decoder_1_out5));
  Transistor #(.\type ("n")) transistor_11 (.in(1'b1), .out(pull_resistor_9_node[3]), .gate(decoder_1_out6));
  Transistor #(.\type ("n")) transistor_12 (.in(1'b1), .out(pull_resistor_9_node[3]), .gate(decoder_1_out7));
  Pull_Resistor pull_resistor_3 (.node(transistor_33_out[3]));
  Transistor #(.\type ("n")) transistor_13 (.in(1'b1), .out(transistor_33_out[3]), .gate(decoder_2_out3));
  Transistor #(.\type ("n")) transistor_14 (.in(1'b1), .out(transistor_33_out[3]), .gate(decoder_2_out5));
  Transistor #(.\type ("n")) transistor_15 (.in(1'b1), .out(transistor_33_out[3]), .gate(decoder_2_out6));
  Transistor #(.\type ("n")) transistor_16 (.in(1'b1), .out(transistor_33_out[3]), .gate(decoder_2_out7));
  Pull_Resistor pull_resistor_4 (.node(pull_resistor_9_node[3]));
  Pull_Resistor pull_resistor_5 (.node(pull_resistor_9_node[2]));
  Transistor #(.\type ("n")) transistor_17 (.in(1'b1), .out(pull_resistor_9_node[2]), .gate(decoder_1_out2));
  Transistor #(.\type ("n")) transistor_18 (.in(1'b1), .out(pull_resistor_9_node[2]), .gate(decoder_1_out3));
  Transistor #(.\type ("n")) transistor_19 (.in(1'b1), .out(pull_resistor_9_node[2]), .gate(decoder_1_out4));
  Transistor #(.\type ("n")) transistor_20 (.in(1'b1), .out(pull_resistor_9_node[2]), .gate(decoder_1_out5));
  Transistor #(.\type ("n")) transistor_21 (.in(1'b1), .out(pull_resistor_9_node[2]), .gate(decoder_1_out6));
  Transistor #(.\type ("n")) transistor_22 (.in(1'b1), .out(pull_resistor_9_node[2]), .gate(decoder_1_out7));
  Pull_Resistor pull_resistor_6 (.node(transistor_33_out[2]));
  Transistor #(.\type ("n")) transistor_23 (.in(1'b1), .out(transistor_33_out[2]), .gate(decoder_2_out2));
  Transistor #(.\type ("n")) transistor_24 (.in(1'b1), .out(transistor_33_out[2]), .gate(decoder_2_out3));
  Transistor #(.\type ("n")) transistor_25 (.in(1'b1), .out(transistor_33_out[2]), .gate(decoder_2_out4));
  Transistor #(.\type ("n")) transistor_26 (.in(1'b1), .out(transistor_33_out[2]), .gate(decoder_2_out5));
  Transistor #(.\type ("n")) transistor_27 (.in(1'b1), .out(transistor_33_out[2]), .gate(decoder_2_out6));
  Transistor #(.\type ("n")) transistor_28 (.in(1'b1), .out(transistor_33_out[2]), .gate(decoder_2_out7));
  Transistor #(.\type ("n")) transistor_29 (.in(1'b1), .out(pull_resistor_9_node[1]), .gate(decoder_1_out6));
  Transistor #(.\type ("n")) transistor_30 (.in(1'b1), .out(pull_resistor_9_node[1]), .gate(decoder_1_out7));
  Pull_Resistor pull_resistor_7 (.node(transistor_33_out[1]));
  Transistor #(.\type ("n")) transistor_31 (.in(1'b1), .out(transistor_33_out[1]), .gate(decoder_2_out6));
  Transistor #(.\type ("n")) transistor_32 (.in(1'b1), .out(transistor_33_out[1]), .gate(decoder_2_out7));
  Pull_Resistor pull_resistor_8 (.node(pull_resistor_9_node[1]));
  Transistor #(.\type ("n")) transistor_33 (.in(1'b1), .out(transistor_33_out[0]), .gate(decoder_2_out1));
  Pull_Resistor pull_resistor_9 (.node(pull_resistor_9_node[0]));
  Transistor #(.\type ("n")) transistor_34 (.in(1'b1), .out(pull_resistor_9_node[0]), .gate(decoder_1_out0));
  Transistor #(.\type ("n")) transistor_35 (.in(1'b1), .out(pull_resistor_9_node[0]), .gate(decoder_1_out1));
  Transistor #(.\type ("n")) transistor_36 (.in(1'b1), .out(pull_resistor_9_node[0]), .gate(decoder_1_out2));
  Transistor #(.\type ("n")) transistor_37 (.in(1'b1), .out(pull_resistor_9_node[0]), .gate(decoder_1_out3));
  Pull_Resistor pull_resistor_10 (.node(transistor_33_out[0]));
  Transistor #(.\type ("n")) transistor_38 (.in(1'b1), .out(transistor_33_out[0]), .gate(decoder_2_out0));
  Transistor #(.\type ("n")) transistor_39 (.in(1'b1), .out(transistor_33_out[0]), .gate(decoder_2_out2));
  Transistor #(.\type ("n")) transistor_40 (.in(1'b1), .out(transistor_33_out[0]), .gate(decoder_2_out3));
  Decoder #(.select(3), .enable("false")) decoder_3 (
    .out0(decoder_3_out0), .out1(decoder_3_out1), .out2(decoder_3_out2), .out3(decoder_3_out3),
    .out4(decoder_3_out4), .out5(decoder_3_out5), .out6(decoder_3_out6), .out7(decoder_3_out7),
    .sel({A[3], B[3], and_3_out[0]}));
  Decoder #(.select(3), .enable("false")) decoder_4 (
    .out0(decoder_4_out0), .out1(decoder_4_out1), .out2(decoder_4_out2), .out3(decoder_4_out3),
    .out4(decoder_4_out4), .out5(decoder_4_out5), .out6(decoder_4_out6), .out7(decoder_4_out7),
    .sel({A[2], B[2], and_2_out[0]}));
  Pull_Resistor pull_resistor_11 (.node(transistor_73_out[4]));
  Transistor #(.\type ("n")) transistor_41 (.in(1'b1), .out(transistor_73_out[4]), .gate(decoder_3_out1));
  Transistor #(.\type ("n")) transistor_42 (.in(1'b1), .out(transistor_73_out[4]), .gate(decoder_3_out2));
  Transistor #(.\type ("n")) transistor_43 (.in(1'b1), .out(transistor_73_out[4]), .gate(decoder_3_out4));
  Transistor #(.\type ("n")) transistor_44 (.in(1'b1), .out(transistor_73_out[4]), .gate(decoder_3_out7));
  Pull_Resistor pull_resistor_12 (.node(pull_resistor_20_node[4]));
  Transistor #(.\type ("n")) transistor_45 (.in(1'b1), .out(pull_resistor_20_node[4]), .gate(decoder_4_out1));
  Transistor #(.\type ("n")) transistor_46 (.in(1'b1), .out(pull_resistor_20_node[4]), .gate(decoder_4_out2));
  Transistor #(.\type ("n")) transistor_47 (.in(1'b1), .out(pull_resistor_20_node[4]), .gate(decoder_4_out4));
  Transistor #(.\type ("n")) transistor_48 (.in(1'b1), .out(pull_resistor_20_node[4]), .gate(decoder_4_out7));
  Pull_Resistor pull_resistor_13 (.node(transistor_73_out[3]));
  Transistor #(.\type ("n")) transistor_49 (.in(1'b1), .out(transistor_73_out[3]), .gate(decoder_3_out3));
  Transistor #(.\type ("n")) transistor_50 (.in(1'b1), .out(transistor_73_out[3]), .gate(decoder_3_out5));
  Transistor #(.\type ("n")) transistor_51 (.in(1'b1), .out(transistor_73_out[3]), .gate(decoder_3_out6));
  Transistor #(.\type ("n")) transistor_52 (.in(1'b1), .out(transistor_73_out[3]), .gate(decoder_3_out7));
  Transistor #(.\type ("n")) transistor_53 (.in(1'b1), .out(pull_resistor_20_node[3]), .gate(decoder_4_out3));
  Transistor #(.\type ("n")) transistor_54 (.in(1'b1), .out(pull_resistor_20_node[3]), .gate(decoder_4_out5));
  Transistor #(.\type ("n")) transistor_55 (.in(1'b1), .out(pull_resistor_20_node[3]), .gate(decoder_4_out6));
  Transistor #(.\type ("n")) transistor_56 (.in(1'b1), .out(pull_resistor_20_node[3]), .gate(decoder_4_out7));
  Pull_Resistor pull_resistor_14 (.node(pull_resistor_20_node[3]));
  Pull_Resistor pull_resistor_15 (.node(transistor_73_out[2]));
  Transistor #(.\type ("n")) transistor_57 (.in(1'b1), .out(transistor_73_out[2]), .gate(decoder_3_out2));
  Transistor #(.\type ("n")) transistor_58 (.in(1'b1), .out(transistor_73_out[2]), .gate(decoder_3_out3));
  Transistor #(.\type ("n")) transistor_59 (.in(1'b1), .out(transistor_73_out[2]), .gate(decoder_3_out4));
  Transistor #(.\type ("n")) transistor_60 (.in(1'b1), .out(transistor_73_out[2]), .gate(decoder_3_out5));
  Transistor #(.\type ("n")) transistor_61 (.in(1'b1), .out(transistor_73_out[2]), .gate(decoder_3_out6));
  Transistor #(.\type ("n")) transistor_62 (.in(1'b1), .out(transistor_73_out[2]), .gate(decoder_3_out7));
  Pull_Resistor pull_resistor_16 (.node(pull_resistor_20_node[2]));
  Transistor #(.\type ("n")) transistor_63 (.in(1'b1), .out(pull_resistor_20_node[2]), .gate(decoder_4_out2));
  Transistor #(.\type ("n")) transistor_64 (.in(1'b1), .out(pull_resistor_20_node[2]), .gate(decoder_4_out3));
  Transistor #(.\type ("n")) transistor_65 (.in(1'b1), .out(pull_resistor_20_node[2]), .gate(decoder_4_out4));
  Transistor #(.\type ("n")) transistor_66 (.in(1'b1), .out(pull_resistor_20_node[2]), .gate(decoder_4_out5));
  Transistor #(.\type ("n")) transistor_67 (.in(1'b1), .out(pull_resistor_20_node[2]), .gate(decoder_4_out6));
  Transistor #(.\type ("n")) transistor_68 (.in(1'b1), .out(pull_resistor_20_node[2]), .gate(decoder_4_out7));
  Pull_Resistor pull_resistor_17 (.node(transistor_73_out[1]));
  Transistor #(.\type ("n")) transistor_69 (.in(1'b1), .out(transistor_73_out[1]), .gate(decoder_3_out6));
  Transistor #(.\type ("n")) transistor_70 (.in(1'b1), .out(transistor_73_out[1]), .gate(decoder_3_out7));
  Transistor #(.\type ("n")) transistor_71 (.in(1'b1), .out(pull_resistor_20_node[1]), .gate(decoder_4_out6));
  Transistor #(.\type ("n")) transistor_72 (.in(1'b1), .out(pull_resistor_20_node[1]), .gate(decoder_4_out7));
  Transistor #(.\type ("n")) transistor_73 (.in(1'b1), .out(transistor_73_out[0]), .gate(decoder_3_out1));
  Pull_Resistor pull_resistor_18 (.node(pull_resistor_20_node[1]));
  Pull_Resistor pull_resistor_19 (.node(transistor_73_out[0]));
  Transistor #(.\type ("n")) transistor_74 (.in(1'b1), .out(transistor_73_out[0]), .gate(decoder_3_out0));
  Transistor #(.\type ("n")) transistor_75 (.in(1'b1), .out(transistor_73_out[0]), .gate(decoder_3_out2));
  Transistor #(.\type ("n")) transistor_76 (.in(1'b1), .out(transistor_73_out[0]), .gate(decoder_3_out3));
  Pull_Resistor pull_resistor_20 (.node(pull_resistor_20_node[0]));
  Transistor #(.\type ("n")) transistor_77 (.in(1'b1), .out(pull_resistor_20_node[0]), .gate(decoder_4_out0));
  Transistor #(.\type ("n")) transistor_78 (.in(1'b1), .out(pull_resistor_20_node[0]), .gate(decoder_4_out1));
  Transistor #(.\type ("n")) transistor_79 (.in(1'b1), .out(pull_resistor_20_node[0]), .gate(decoder_4_out2));
  Transistor #(.\type ("n")) transistor_80 (.in(1'b1), .out(pull_resistor_20_node[0]), .gate(decoder_4_out3));
  Decoder #(.select(2), .enable("false")) decoder_5 (
    .out0(decoder_5_out0), .out1(decoder_5_out1), .out2(decoder_5_out2), .out3(decoder_5_out3), .sel({Z, D}));
  Pull_Resistor pull_resistor_21 (.node(ADR[7]));
  Transistor #(.\type ("n")) transistor_81 (.in(1'b1), .out(ADR[7]), .gate(decoder_5_out2));
  Transistor #(.\type ("n")) transistor_82 (.in(1'b1), .out(ADR[7]), .gate(decoder_5_out3));
  Transistor #(.\type ("n")) transistor_83 (.in(1'b1), .out(ADR[6]), .gate(decoder_5_out2));
  Transistor #(.\type ("n")) transistor_84 (.in(1'b1), .out(ADR[6]), .gate(decoder_5_out3));
  Pull_Resistor pull_resistor_22 (.node(ADR[6]));
  Pull_Resistor pull_resistor_23 (.node(ADR[5]));
  Transistor #(.\type ("n")) transistor_85 (.in(1'b1), .out(ADR[5]), .gate(decoder_5_out3));
  Pull_Resistor pull_resistor_24 (.node(ADR[4]));
  Transistor #(.\type ("n")) transistor_86 (.in(1'b1), .out(ADR[4]), .gate(decoder_5_out3));
  Transistor #(.\type ("n")) transistor_87 (.in(1'b1), .out(ADR[3]), .gate(decoder_5_out1));
  Transistor #(.\type ("n")) transistor_88 (.in(1'b1), .out(ADR[3]), .gate(decoder_5_out3));
  Pull_Resistor pull_resistor_25 (.node(ADR[3]));
  Pull_Resistor pull_resistor_26 (.node(ADR[2]));
  Transistor #(.\type ("n")) transistor_89 (.in(1'b1), .out(ADR[2]), .gate(decoder_5_out1));
  Transistor #(.\type ("n")) transistor_90 (.in(1'b1), .out(ADR[2]), .gate(decoder_5_out3));
  Pull_Resistor pull_resistor_27 (.node(ADR[1]));
  Transistor #(.\type ("n")) transistor_91 (.in(1'b1), .out(ADR[1]), .gate(decoder_5_out1));
  Pull_Resistor pull_resistor_28 (.node(ADR[0]));
  Transistor #(.\type ("n")) transistor_92 (.in(1'b1), .out(ADR[0]), .gate(decoder_5_out1));
endmodule
