// Logisim project Exo2__TD1.circ as structural Verilog: 3 circuits, main circuit Exemple1
module Exemple1 (
  input  [20:0] in_1,
  input  in_2,
  input  in_3,
  output [7:0] out_4
);

  wire clock_1_out, decoder_1_out0, decoder_1_out1, decoder_1_out2, decoder_1_out3;

  Decoder #(.select(2), .enable("false")) decoder_1 (
    .out0(decoder_1_out0), .out1(decoder_1_out1), .out2(decoder_1_out2), .out3(decoder_1_out3),
    .sel(in_1[20:19]));
  Clock clock_1 (.out(clock_1_out));
  RAM #(.addrWidth(19)) ram_1 (
    .addr(in_1[18:0]), .data(out_4), .sel(decoder_1_out0), .clk(clock_1_out), .ld(in_3), .clr(in_2));
  RAM #(.addrWidth(19)) ram_2 (
    .addr(in_1[18:0]), .data(out_4), .sel(decoder_1_out1), .clk(clock_1_out), .ld(in_3), .clr(in_2));
  RAM #(.addrWidth(19)) ram_3 (
    .addr(in_1[18:0]), .data(out_4), .sel(decoder_1_out2), .clk(clock_1_out), .ld(in_3), .clr(in_2));
  RAM #(.addrWidth(19)) ram_4 (
    .addr(in_1[18:0]), .data(out_4), .sel(decoder_1_out3), .clk(clock_1_out), .ld(in_3), .clr(in_2));
endmodule

module Exemple2 (
  input  [20:0] in_1,
  input  in_2,
  input  in_3,
  input  in_4,
  output [3:0] out_5,
  output [3:0] out_6
);

  wire clock_1_out;

  Clock clock_1 (.out(clock_1_out));
  RAM #(.addrWidth(21), .dataWidth(4)) ram_1 (
    .addr(in_1), .data(out_5), .sel(in_3), .clk(clock_1_out), .ld(in_2), .clr(in_4));
  RAM #(.addrWidth(21), .dataWidth(4)) ram_2 (
    .addr(in_1), .data(out_6), .sel(in_3), .clk(clock_1_out), .ld(in_2), .clr(in_4));
endmodule

module Exemple3 (
  input  [20:0] in_1,
  input  in_2,
  input  in_3,
  output [3:0] out_4,
  output [3:0] out_5
);

  wire clock_1_out, decoder_1_out0, decoder_1_out1, decoder_1_out2, decoder_1_out3, decoder_1_out4,
       decoder_1_out5, decoder_1_out6, decoder_1_out7;

  Decoder #(.select(3), .enable("false")) decoder_1 (
    .out0(decoder_1_out0), .out1(decoder_1_out1), .out2(decoder_1_out2), .out3(decoder_1_out3),
    .out4(decoder_1_out4), .out5(decoder_1_out5), .out6(decoder_1_out6), .out7(decoder_1_out7),
    .sel(in_1[20:18]));
  Clock clock_1 (.out(clock_1_out));
  RAM #(.addrWidth(18), .dataWidth(4)) ram_1 (
    .addr(in_1[17:0]), .data(out_4), .sel(decoder_1_out0), .clk(clock_1_out), .ld(in_3), .clr(in_2));
  RAM #(.addrWidth(18), .dataWidth(4)) ram_2 (
    .addr(in_1[17:0]), .data(out_4), .sel(decoder_1_out1), .clk(clock_1_out), .ld(in_3), .clr(in_2));
  RAM #(.addrWidth(18), .dataWidth(4)) ram_3 (
    .addr(in_1[17:0]), .data(out_4), .sel(decoder_1_out2), .clk(clock_1_out), .ld(in_3), .clr(in_2));
  RAM #(.addrWidth(18), .dataWidth(4)) ram_4 (
    .addr(in_1[17:0]), .data(out_4), .sel(decoder_1_out3), .clk(clock_1_out), .ld(in_3), .clr(in_2));
  RAM #(.addrWidth(18), .dataWidth(4)) ram_5 (
    .addr(in_1[17:0]), .data(out_4), .sel(decoder_1_out4), .clk(clock_1_out), .ld(in_3), .clr(in_2));
  RAM #(.addrWidth(18), .dataWidth(4)) ram_6 (
    .addr(in_1[17:0]), .data(out_4), .sel(decoder_1_out5), .clk(clock_1_out), .ld(in_3), .clr(in_2));
  RAM #(.addrWidth(18), .dataWidth(4)) ram_7 (
    .addr(in_1[17:0]), .data(out_4), .sel(decoder_1_out6), .clk(clock_1_out), .ld(in_3), .clr(in_2));
  RAM #(.addrWidth(18), .dataWidth(4)) ram_8 (
    .addr(in_1[17:0]), .data(out_4), .sel(decoder_1_out7), .clk(clock_1_out), .ld(in_3), .clr(in_2));
  RAM #(.addrWidth(18), .dataWidth(4)) ram_9 (
    .addr(in_1[17:0]), .data(out_5), .sel(decoder_1_out0), .clk(clock_1_out), .ld(in_3), .clr(in_2));
  RAM #(.addrWidth(18), .dataWidth(4)) ram_10 (
    .addr(in_1[17:0]), .data(out_5), .sel(decoder_1_out1), .clk(clock_1_out), .ld(in_3), .clr(in_2));
  RAM #(.addrWidth(18), .dataWidth(4)) ram_11 (
    .addr(in_1[17:0]), .data(out_5), .sel(decoder_1_out2), .clk(clock_1_out), .ld(in_3), .clr(in_2));
  RAM #(.addrWidth(18), .dataWidth(4)) ram_12 (
    .addr(in_1[17:0]), .data(out_5), .sel(decoder_1_out3), .clk(clock_1_out), .ld(in_3), .clr(in_2));
  RAM #(.addrWidth(18), .dataWidth(4)) ram_13 (
    .addr(in_1[17:0]), .data(out_5), .sel(decoder_1_out4), .clk(clock_1_out), .ld(in_3), .clr(in_2));
  RAM #(.addrWidth(18), .dataWidth(4)) ram_14 (
    .addr(in_1[17:0]), .data(out_5), .sel(decoder_1_out5), .clk(clock_1_out), .ld(in_3), .clr(in_2));
  RAM #(.addrWidth(18), .dataWidth(4)) ram_15 (
    .addr(in_1[17:0]), .data(out_5), .sel(decoder_1_out6), .clk(clock_1_out), .ld(in_3), .clr(in_2));
  RAM #(.addrWidth(18), .dataWidth(4)) ram_16 (
    .addr(in_1[17:0]), .data(out_5), .sel(decoder_1_out7), .clk(clock_1_out), .ld(in_3), .clr(in_2));
endmodule
