// Logisim project Exo3__TD1.circ as structural Verilog: 1 circuit, main circuit main
module main (
  input  [10:0] in_1,
  input  in_2,
  input  in_3,
  output [7:0] out_4
);

  wire and_1_out, and_2_out, and_3_out, and_4_out, and_5_out, and_6_out, and_7_out, and_8_out, clock_2_out,
       decoder_1_out0, decoder_1_out1, decoder_2_out0, decoder_2_out1, decoder_2_out2, decoder_2_out3;

  Decoder #(.enable("false")) decoder_1 (.out0(decoder_1_out0), .out1(decoder_1_out1), .sel(in_1[10]));
  Decoder #(.select(2), .enable("false")) decoder_2 (
    .out0(decoder_2_out0), .out1(decoder_2_out1), .out2(decoder_2_out2), .out3(decoder_2_out3),
    .sel(in_1[1:0]));
  and and_1 (and_1_out, decoder_2_out0, decoder_1_out0);
  RAM ram_1 (.addr(in_1[9:2]), .data(out_4), .sel(and_7_out), .clk(clock_2_out), .ld(in_3), .clr(in_2));
  RAM ram_2 (.addr(in_1[9:2]), .data(out_4), .sel(and_8_out), .clk(clock_2_out), .ld(in_3), .clr(in_2));
  and and_2 (and_2_out, decoder_2_out0, decoder_1_out1);
  and and_3 (and_3_out, decoder_2_out1, decoder_1_out0);
  Clock clock_1 ();  // open: out
  and and_4 (and_4_out, decoder_2_out1, decoder_1_out1);
  RAM ram_3 (.addr(in_1[9:2]), .data(out_4), .sel(and_5_out), .clk(clock_2_out), .ld(in_3), .clr(in_2));
  RAM ram_4 (.addr(in_1[9:2]), .data(out_4), .sel(and_6_out), .clk(clock_2_out), .ld(in_3), .clr(in_2));
  buf and_5 (and_5_out, decoder_2_out2);  // AND_Gate
  and and_6 (and_6_out, decoder_2_out2, decoder_1_out1);
  and and_7 (and_7_out, decoder_2_out3, decoder_1_out0);
  RAM ram_5 (.addr(in_1[9:2]), .data(out_4), .sel(and_3_out), .clk(clock_2_out), .ld(in_3), .clr(in_2));
  RAM ram_6 (.addr(in_1[9:2]), .data(out_4), .sel(and_4_out), .clk(clock_2_out), .ld(in_3), .clr(in_2));
  and and_8 (and_8_out, decoder_2_out3, decoder_1_out1);
  RAM ram_7 (.addr(in_1[9:2]), .data(out_4), .sel(and_1_out), .clk(clock_2_out), .ld(in_3), .clr(in_2));
  RAM ram_8 (.addr(in_1[9:2]), .data(out_4), .sel(and_2_out), .clk(clock_2_out), .ld(in_3), .clr(in_2));
  Clock clock_2 (.out(clock_2_out));
endmodule
