// Logisim project Exo4__TD1.circ as structural Verilog: 1 circuit, main circuit main
module main (
  input  [11:0] in_1,
  input  in_2,
  input  in_3,
  input  in_4,
  input  in_5
);

  wire and_1_out, and_2_out, and_3_out, and_4_out, and_5_out, and_6_out, and_7_out, and_8_out, and_9_out,
       and_10_out, and_11_out, and_12_out, and_13_out, and_14_out, and_15_out, and_16_out, and_17_out,
       and_18_out, and_19_out, and_20_out, and_21_out, and_22_out, and_23_out, and_24_out, clock_1_out,
       clock_2_out, decoder_1_out0, decoder_1_out1, decoder_2_out0, decoder_2_out1, decoder_3_out0,
       decoder_3_out1, decoder_3_out2, decoder_3_out3;

  Decoder #(.enable("false")) decoder_1 (.out0(decoder_1_out0), .out1(decoder_1_out1), .sel(in_1[10]));
  Decoder #(.enable("false")) decoder_2 (.out0(decoder_2_out0), .out1(decoder_2_out1), .sel(in_1[11]));
  Decoder #(.select(2), .enable("false")) decoder_3 (
    .out0(decoder_3_out0), .out1(decoder_3_out1), .out2(decoder_3_out2), .out3(decoder_3_out3),
    .sel(in_1[1:0]));
  RAM #(.dataWidth(4)) ram_1 (
    .addr(in_1[9:2]), .sel(and_21_out), .clk(clock_1_out), .ld(in_2), .clr(in_3));  // open: data
  RAM #(.dataWidth(4)) ram_2 (
    .addr(in_1[9:2]), .sel(and_22_out), .clk(clock_1_out), .ld(in_2), .clr(in_3));  // open: data
  and and_1 (and_1_out, decoder_3_out0, decoder_2_out0);
  and and_2 (and_2_out, decoder_3_out0, decoder_2_out1);
  RAM #(.dataWidth(4)) ram_3 (
    .addr(in_1[9:2]), .sel(and_23_out), .clk(clock_2_out), .ld(in_4), .clr(in_5));  // open: data
  RAM #(.dataWidth(4)) ram_4 (
    .addr(in_1[9:2]), .sel(and_24_out), .clk(clock_2_out), .ld(in_4), .clr(in_5));  // open: data
  and and_3 (and_3_out, decoder_3_out1, decoder_2_out0);
  RAM #(.dataWidth(4)) ram_5 (
    .addr(in_1[9:2]), .sel(and_17_out), .clk(clock_1_out), .ld(in_2), .clr(in_3));  // open: data
  RAM #(.dataWidth(4)) ram_6 (
    .addr(in_1[9:2]), .sel(and_18_out), .clk(clock_1_out), .ld(in_2), .clr(in_3));  // open: data
  and and_4 (and_4_out, decoder_3_out1, decoder_2_out1);
  and and_5 (and_5_out, decoder_3_out2, decoder_2_out0);
  RAM #(.dataWidth(4)) ram_7 (
    .addr(in_1[9:2]), .sel(and_19_out), .clk(clock_2_out), .ld(in_4), .clr(in_5));  // open: data
  RAM #(.dataWidth(4)) ram_8 (
    .addr(in_1[9:2]), .sel(and_20_out), .clk(clock_2_out), .ld(in_4), .clr(in_5));  // open: data
  and and_6 (and_6_out, decoder_3_out2, decoder_2_out1);
  RAM #(.dataWidth(4)) ram_9 (
    .addr(in_1[9:2]), .sel(and_13_out), .clk(clock_1_out), .ld(in_2), .clr(in_3));  // open: data
  RAM #(.dataWidth(4)) ram_10 (
    .addr(in_1[9:2]), .sel(and_14_out), .clk(clock_1_out), .ld(in_2), .clr(in_3));  // open: data
  and and_7 (and_7_out, decoder_3_out3, decoder_2_out0);
  RAM #(.dataWidth(4)) ram_11 (
    .addr(in_1[9:2]), .sel(and_15_out), .clk(clock_2_out), .ld(in_4), .clr(in_5));  // open: data
  RAM #(.dataWidth(4)) ram_12 (
    .addr(in_1[9:2]), .sel(and_16_out), .clk(clock_2_out), .ld(in_4), .clr(in_5));  // open: data
  and and_8 (and_8_out, decoder_3_out3, decoder_2_out1);
  RAM #(.dataWidth(4)) ram_13 (
    .addr(in_1[9:2]), .sel(and_9_out), .clk(clock_1_out), .ld(in_2), .clr(in_3));  // open: data
  RAM #(.dataWidth(4)) ram_14 (
    .addr(in_1[9:2]), .sel(and_10_out), .clk(clock_1_out), .ld(in_2), .clr(in_3));  // open: data
  RAM #(.dataWidth(4)) ram_15 (
    .addr(in_1[9:2]), .sel(and_11_out), .clk(clock_2_out), .ld(in_4), .clr(in_5));  // open: data
  RAM #(.dataWidth(4)) ram_16 (
    .addr(in_1[9:2]), .sel(and_12_out), .clk(clock_2_out), .ld(in_4), .clr(in_5));  // open: data
  Clock clock_1 (.out(clock_1_out));
  Clock clock_2 (.out(clock_2_out));
  and and_9 (and_9_out, and_1_out, decoder_1_out0);
  and and_10 (and_10_out, and_1_out, decoder_1_out1);
  and and_11 (and_11_out, and_2_out, decoder_1_out0);
  and and_12 (and_12_out, and_2_out, decoder_1_out1);
  and and_13 (and_13_out, and_3_out, decoder_1_out0);
  and and_14 (and_14_out, and_3_out, decoder_1_out1);
  and and_15 (and_15_out, and_4_out, decoder_1_out0);
  and and_16 (and_16_out, and_4_out, decoder_1_out1);
  and and_17 (and_17_out, and_5_out, decoder_1_out0);
  and and_18 (and_18_out, and_5_out, decoder_1_out1);
  and and_19 (and_19_out, and_6_out, decoder_1_out0);
  and and_20 (and_20_out, and_6_out, decoder_1_out1);
  and and_21 (and_21_out, and_7_out, decoder_1_out0);
  and and_22 (and_22_out, and_7_out, decoder_1_out1);
  and and_23 (and_23_out, and_8_out, decoder_1_out0);
  and and_24 (and_24_out, and_8_out, decoder_1_out1);

  // Notes on the sheet:
  //   adersse
  //   module
  //   boitiers
  //   bloc
endmodule
