// Logisim project TD_6_EXO_5,6_.circ as structural Verilog: 2 circuits, main circuit EXO5
module EXO5 (
  output [1:0] out_1
);

  wire and_1_out, and_2_out, and_3_out, and_4_out, clock_1_out, controlled_buffer_1_out,
       controlled_buffer_2_out, controlled_buffer_3_out, controlled_buffer_4_out, d_ff_1_q, d_ff_2_q,
       d_ff_3_q, d_ff_4_q, decoder_1_out0, decoder_1_out1, decoder_1_out2, decoder_1_out3, not_1_out,
       not_2_out, not_3_out, not_4_out, or_1_out, or_2_out, or_3_out, or_4_out;

  Clock clock_1 (.out(clock_1_out));
  D_Flip_Flop d_ff_1 (.clk(clock_1_out), .D(controlled_buffer_2_out), .Q(d_ff_1_q));  // open: Qn, preset, en, reset
  or or_1 (or_1_out, d_ff_1_q, 1'b0);
  not not_1 (not_1_out, 1'b0);
  and and_1 (and_1_out, not_1_out, d_ff_1_q);
  D_Flip_Flop d_ff_2 (.clk(clock_1_out), .D(controlled_buffer_3_out), .Q(d_ff_2_q));  // open: Qn, preset, en, reset
  or or_2 (or_2_out, d_ff_2_q, or_1_out);
  not not_2 (not_2_out, or_1_out);
  and and_2 (and_2_out, not_2_out, d_ff_2_q);
  D_Flip_Flop d_ff_3 (.clk(clock_1_out), .D(controlled_buffer_4_out), .Q(d_ff_3_q));  // open: Qn, preset, en, reset
  or or_3 (or_3_out, d_ff_3_q, or_2_out);
  not not_3 (not_3_out, or_2_out);
  and and_3 (and_3_out, not_3_out, d_ff_3_q);
  assign controlled_buffer_1_out = decoder_1_out3 ? 1'b0 : 1'bz;  // Controlled_Buffer controlled_buffer_1
  D_Flip_Flop d_ff_4 (.clk(clock_1_out), .D(controlled_buffer_1_out), .Q(d_ff_4_q));  // open: Qn, preset, en, reset
  not not_4 (not_4_out, or_3_out);
  assign controlled_buffer_2_out = decoder_1_out0 ? 1'b0 : 1'bz;  // Controlled_Buffer controlled_buffer_2
  assign controlled_buffer_3_out = decoder_1_out1 ? 1'b0 : 1'bz;  // Controlled_Buffer controlled_buffer_3
  assign controlled_buffer_4_out = decoder_1_out2 ? 1'b0 : 1'bz;  // Controlled_Buffer controlled_buffer_4
  or or_4 (or_4_out, d_ff_4_q, or_3_out);
  and and_4 (and_4_out, not_4_out, d_ff_4_q);
  Priority_Encoder #(.select(2)) priority_encoder_1 (
    .in0(and_1_out), .in1(and_2_out), .in2(and_3_out), .in3(and_4_out), .out(out_1), .en_in(or_4_out));  // open: gs, en_out
  Decoder #(.select(2), .enable("false")) decoder_1 (
    .out0(decoder_1_out0), .out1(decoder_1_out1), .out2(decoder_1_out2), .out3(decoder_1_out3), .sel(out_1));

  // Notes on the sheet:
  //   signal  d'acquittement = 0
  //   CT0
  //   CT1
  //   CT2
  //   CT3
endmodule

module EXO6 (
  input  Couse_0,
  input  Couse_1,
  input  in_3,
  input  in_4,
  input  Couse_0_2,
  input  Couse_1_2,
  input  Couse_2,
  input  Couse_3,
  input  in_9,
  input  in_10,
  input  in_11,
  input  in_12,
  input  Couse_0_3,
  input  Couse_1_3,
  input  Couse_2_2,
  input  Couse_3_2,
  input  in_17,
  input  in_18,
  input  in_19,
  input  in_20,
  input  in_21,
  input  in_22,
  input  in_23,
  input  in_24,
  input  Couse_0_4,
  input  Couse_1_4,
  input  Couse_2_3,
  input  in_28,
  input  in_29,
  input  Couse_4,
  input  in_31,
  input  in_32,
  input  in_33,
  input  in_34,
  input  in_35,
  input  in_36
);

  wire and_1_out, clock_1_out, d_ff_2_q, or_1_out, or_2_out, or_3_out, or_4_out, or_5_out;
  wire [1:0] and_12_out, register_5_q;
  wire [3:0] and_2_out, and_14_out, and_18_out, register_1_q, register_2_q, register_3_q;
  wire [5:0] and_6_out, register_4_q;

  D_Flip_Flop d_ff_1 (.clk(clock_1_out), .D(and_1_out));  // open: Q, Qn, preset, en, reset
  Clock clock_1 (.out(clock_1_out));
  and and_1 (and_1_out, or_1_out, d_ff_2_q);
  D_Flip_Flop d_ff_2 (.Q(d_ff_2_q));  // open: clk, D, Qn, preset, en, reset
  or or_1 (or_1_out, register_1_q[0], register_1_q[1], register_1_q[2], register_1_q[3]);
  Register #(.width(4)) register_1 (.D(and_2_out), .Q(register_1_q), .clk(clock_1_out));  // open: en, clr
  and and_2 (and_2_out[0], or_2_out, in_20);
  and and_3 (and_2_out[1], or_3_out, in_19);
  and and_4 (and_2_out[2], or_4_out, in_18);
  and and_5 (and_2_out[3], or_5_out, in_17);
  or or_2 (or_2_out, register_5_q[0], register_5_q[1]);
  or or_3 (or_3_out, register_2_q[0], register_2_q[1], register_2_q[2], register_2_q[3]);
  or or_4 (or_4_out, register_3_q[0], register_3_q[1], register_3_q[2], register_3_q[3]);
  or or_5 (or_5_out, register_4_q[0], register_4_q[1], register_4_q[2], register_4_q[3], register_4_q[4], register_4_q[5]);
  Register #(.width(4)) register_2 (.D(and_14_out), .Q(register_2_q), .clk(clock_1_out));  // open: en, clr
  Register #(.width(4)) register_3 (.D(and_18_out), .Q(register_3_q), .clk(clock_1_out));  // open: en, clr
  Register #(.width(6)) register_4 (.D(and_6_out), .Q(register_4_q), .clk(clock_1_out));  // open: en, clr
  Register #(.width(2)) register_5 (.D(and_12_out), .Q(register_5_q), .clk(clock_1_out));  // open: en, clr
  and and_6 (and_6_out[0], Couse_0_4, in_36);
  and and_7 (and_6_out[1], Couse_1_4, in_35);
  and and_8 (and_6_out[2], Couse_2_3, in_34);
  and and_9 (and_6_out[3], in_28, in_33);
  and and_10 (and_6_out[4], in_29, in_32);
  and and_11 (and_6_out[5], Couse_4, in_31);
  and and_12 (and_12_out[0], Couse_0, in_4);
  and and_13 (and_12_out[1], Couse_1, in_3);
  and and_14 (and_14_out[0], Couse_0_2, in_12);
  and and_15 (and_14_out[1], Couse_1_2, in_11);
  and and_16 (and_14_out[2], Couse_2, in_10);
  and and_17 (and_14_out[3], Couse_3, in_9);
  and and_18 (and_18_out[0], Couse_0_3, in_24);
  and and_19 (and_18_out[1], Couse_1_3, in_23);
  and and_20 (and_18_out[2], Couse_2_2, in_22);
  and and_21 (and_18_out[3], Couse_3_2, in_21);

  // Notes on the sheet:
  //   BI
  //   Au démarrage 1
  //   BV
  //   RM des niveaux
  //   Au démarrage 1111
  //   Registre Masque
  //   RM des couses niveau 3
  //   RM des couses niveau 0
  //   RM des couses niveau 1
  //   RM des couses niveau 2
  //   Registre d'inhibition niveau 0
  //   Registre d'inhibition niveau 3
  //   Registre d'inhibition niveau 1
  //   Registre d'inhibition niveau 2
  //   Au démarrage 11
  //   Au démarrage 0011
  //   Au démarrage 0111
  //   Couse 3
  //   Couse 5
  //   Au démarrage 001111
  //   ( Les pannes du courant ) 
  //   ( Les pannes du matériel )
  //   Disque 0
  //   Disque 1
  //   Disque 2
  //   Disque 3
  //   Périphérique 0
  //   Périphérique 1
  //   Périphérique 2
  //   Périphérique 3
  //   Locaux 0
  //   Locaux 1
  //   Locaux 2
  //   Locaux 3
  //   Locaux 4
  //   Locaux 5
  //   } Niveau 0
  //   } Niveau 1
  //   } Niveau 2
  //   } Niveau 3
endmodule
